// Logisim project hamming.circ as structural Verilog: 1 circuit, main circuit main
module main (
  input  in_1,
  input  in_2,
  input  in_3,
  input  in_4,
  input  in_5,
  input  in_6,
  input  in_7,
  input  in_8,
  input  in_9,
  input  in_10,
  input  in_11,
  input  in_12,
  input  in_13,
  input  in_14,
  input  in_15,
  input  in_16,
  input  in_17,
  input  in_18,
  input  in_19,
  input  in_20,
  input  in_21,
  input  in_22,
  input  in_23,
  input  in_24,
  input  in_25,
  input  in_26,
  input  in_27,
  input  in_28,
  input  in_29,
  input  in_30,
  input  in_31,
  input  in_32,
  input  in_33,
  input  PRN,
  input  PRN_2,
  input  PRN_3,
  input  GND,
  input  PRN_4,
  input  in_39,
  input  PRN_5,
  input  PRN_6,
  input  PRN_7,
  input  PRN_8,
  output out_44,
  output out_45,
  output out_46,
  output out_47,
  output out_48,
  output out_49,
  output out_50,
  output out_51,
  output out_52,
  output out_53,
  output out_54,
  output out_55,
  output out_56,
  output out_57,
  output out_58,
  output out_59,
  output out_60,
  output out_61,
  output out_62,
  output out_63,
  output out_64,
  output out_65,
  output out_66,
  output out_67,
  output out_68,
  output out_69,
  output out_70,
  output out_71,
  output out_72,
  output out_73,
  output out_74,
  output out_75,
  output out_76,
  output out_77,
  output out_78,
  output out_79,
  output out_80,
  output out_81,
  output out_82,
  output out_83,
  output out_84,
  output out_85,
  output out_86,
  output out_87,
  output out_88,
  output out_89,
  output out_90,
  output out_91,
  output out_92,
  output out_93,
  output out_94,
  output out_95,
  output out_96,
  output out_97,
  output out_98,
  output out_99,
  output out_100,
  output out_101,
  output out_102,
  output out_103,
  output out_104,
  output out_105,
  output out_106,
  output out_107,
  output out_108,
  output out_109,
  output out_110,
  output out_111,
  output out_112,
  output out_113,
  output out_114,
  output out_115,
  output out_116,
  output out_117,
  output out_118,
  output out_119,
  output out_120,
  output out_121,
  output out_122,
  output out_123,
  output out_124,
  output out_125,
  output out_126,
  output out_127,
  output out_128,
  output out_129,
  output out_130,
  output out_131,
  output out_132,
  output out_133,
  output out_134,
  output out_135,
  output out_136,
  output out_137,
  output out_138,
  output out_139,
  output TOTAL,
  output out_141,
  output out_142,
  output out_143,
  output out_144,
  output out_145,
  output out_146,
  output out_147,
  output out_148,
  output out_149,
  output out_150,
  output out_151,
  output out_152,
  output out_153,
  output out_154,
  output out_155,
  output out_156,
  output out_157,
  output out_158,
  output out_159,
  output out_160,
  output out_161,
  output out_162,
  output out_163,
  output out_164,
  output out_165,
  output out_166,
  output out_167,
  output out_168,
  output out_169,
  output out_170,
  output out_171,
  output out_172,
  output Q,
  output Q_2,
  output Q_3,
  output Q_4,
  output SUM,
  output SUM_2,
  output SUM_3,
  output SUM_4,
  output Q_5,
  output Q_6,
  output Q_7,
  output Q_8
);

  wire _0000_out, _0001_out, _0010_out, _0011_out, _0100_out, _0101_out, _0110_out, _0111_out, _1000_out,
       _1001_out, _1010_out, _1011_out, _1100_out, _1101_out, _1110_out, _1111_out, and_1_out, and_2_out,
       and_3_out, and_4_out, and_5_out, and_6_out, and_7_out, and_8_out, and_9_out, and_10_out, and_11_out,
       and_12_out, and_13_out, and_14_out, and_15_out, and_16_out, and_17_out, and_18_out, and_19_out,
       and_20_out, and_21_out, and_22_out, and_23_out, and_24_out, and_25_out, and_26_out, and_27_out,
       and_28_out, and_29_out, and_30_out, and_31_out, and_32_out, and_33_out, and_34_out, and_35_out,
       and_36_out, and_37_out, and_38_out, and_39_out, and_40_out, and_41_out, and_43_out, and_44_out,
       and_45_out, and_46_out, and_47_out, and_48_out, and_49_out, and_50_out, and_51_out, and_52_out,
       and_53_out, and_54_out, and_55_out, and_56_out, and_57_out, and_58_out, and_59_out, and_60_out,
       and_61_out, and_62_out, and_63_out, and_64_out, and_65_out, and_66_out, and_67_out, and_68_out,
       and_69_out, and_70_out, and_71_out, and_72_out, and_73_out, and_74_out, and_75_out, and_76_out,
       and_77_out, and_78_out, and_79_out, and_80_out, and_81_out, and_82_out, and_83_out, and_84_out,
       and_85_out, and_86_out, and_87_out, and_88_out, and_89_out, and_90_out, and_91_out, and_92_out,
       and_93_out, and_94_out, and_95_out, and_96_out, and_97_out, and_98_out, and_99_out, and_100_out,
       and_101_out, and_102_out, and_103_out, and_104_out, and_105_out, and_106_out, and_107_out,
       and_108_out, and_109_out, and_110_out, and_111_out, and_112_out, and_113_out, and_114_out,
       and_115_out, and_116_out, and_117_out, and_118_out, and_119_out, and_120_out, and_121_out,
       and_122_out, and_123_out, and_124_out, and_125_out, and_126_out, and_127_out, and_128_out,
       and_129_out, and_130_out, buffer_1_out, buffer_2_out, buffer_3_out, buffer_4_out, buffer_5_out,
       buffer_6_out, buffer_7_out, buffer_8_out, buffer_9_out, buffer_10_out, buffer_11_out, buffer_12_out,
       buffer_13_out, buffer_14_out, buffer_15_out, buffer_16_out, buffer_17_out, buffer_18_out,
       buffer_19_out, buffer_20_out, buffer_21_out, buffer_22_out, buffer_23_out, buffer_24_out,
       buffer_25_out, buffer_26_out, buffer_27_out, buffer_28_out, buffer_29_out, buffer_30_out,
       buffer_31_out, buffer_32_out, buffer_33_out, buffer_34_out, buffer_35_out, buffer_36_out,
       buffer_37_out, buffer_38_out, buffer_39_out, buffer_40_out, buffer_41_out, buffer_42_out,
       buffer_43_out, buffer_44_out, CALC_out, CLK_out, nor_1_out, nor_2_out, nor_3_out, nor_4_out,
       nor_5_out, nor_6_out, nor_7_out, nor_8_out, nor_10_out, nor_12_out, nor_14_out, nor_16_out,
       nor_33_out, nor_34_out, nor_35_out, nor_36_out, nor_37_out, nor_38_out, nor_39_out, nor_40_out,
       nor_42_out, nor_44_out, nor_46_out, nor_48_out, not_1_out, not_2_out, not_3_out, not_4_out, not_5_out,
       not_6_out, not_7_out, not_8_out, not_9_out, not_10_out, not_11_out, not_12_out, not_13_out,
       not_14_out, not_15_out, not_16_out, not_17_out, not_18_out, not_19_out, not_20_out, not_21_out,
       not_22_out, not_23_out, not_24_out, not_25_out, not_26_out, not_27_out, not_28_out, not_29_out,
       not_30_out, not_31_out, not_32_out, not_33_out, not_34_out, not_35_out, not_36_out, not_37_out,
       not_38_out, not_39_out, not_40_out, not_41_out, not_42_out, not_43_out, not_44_out, not_45_out,
       not_46_out, not_47_out, not_48_out, not_49_out, not_50_out, not_51_out, not_52_out, not_53_out,
       not_54_out, not_55_out, not_56_out, not_57_out, not_58_out, not_59_out, not_60_out, not_61_out,
       not_62_out, not_63_out, not_64_out, not_65_out, not_66_out, not_67_out, not_68_out, not_69_out,
       not_70_out, not_71_out, not_72_out, not_73_out, not_74_out, not_75_out, not_76_out, not_77_out,
       not_78_out, not_79_out, not_80_out, not_81_out, not_82_out, not_83_out, not_84_out, not_85_out,
       not_86_out, not_87_out, not_88_out, not_89_out, not_90_out, not_91_out, not_92_out, not_93_out,
       not_94_out, not_95_out, not_96_out, not_97_out, not_98_out, or_1_out, or_2_out, or_3_out, or_4_out,
       or_5_out, or_6_out, or_7_out, or_8_out, or_9_out, or_10_out, or_11_out, or_12_out, or_13_out,
       or_15_out, or_17_out, or_19_out, or_20_out, or_22_out, or_23_out, or_24_out, or_25_out, or_28_out,
       or_29_out, or_30_out, or_31_out, or_32_out, or_33_out, or_34_out, or_35_out, or_36_out, xor_1_out,
       xor_2_out, xor_3_out, xor_4_out, xor_5_out, xor_7_out, xor_9_out, xor_11_out;

  not not_1 (not_1_out, and_21_out);
  Clock CLK (.out(CLK_out));
  and and_1 (and_1_out, not_1_out, CLK_out);
  and and_2 (and_2_out, Q, not_2_out);
  and and_3 (and_3_out, Q_4, and_2_out);
  and and_4 (and_4_out, Q_6, and_3_out);
  not not_2 (not_2_out, in_33);
  xor xor_1 (xor_1_out, Q, not_2_out);
  not not_3 (not_3_out, xor_1_out);
  not not_4 (not_4_out, and_1_out);
  xor xor_2 (xor_2_out, Q_4, and_2_out);
  not not_5 (not_5_out, xor_2_out);
  not not_6 (not_6_out, and_1_out);
  xor xor_3 (xor_3_out, Q_6, and_3_out);
  not not_7 (not_7_out, xor_3_out);
  not not_8 (not_8_out, and_1_out);
  xor xor_4 (xor_4_out, Q_8, and_4_out);
  not not_9 (not_9_out, xor_4_out);
  not not_10 (not_10_out, and_1_out);
  and and_5 (and_5_out, xor_1_out, not_4_out);
  nor nor_1 (nor_1_out, buffer_1_out, and_6_out);
  and and_6 (and_6_out, not_3_out, not_4_out);
  and and_7 (and_7_out, xor_2_out, not_6_out);
  nor nor_2 (nor_2_out, buffer_2_out, and_8_out);
  and and_8 (and_8_out, not_5_out, not_6_out);
  and and_9 (and_9_out, xor_3_out, not_8_out);
  nor nor_3 (nor_3_out, buffer_3_out, and_10_out);
  and and_10 (and_10_out, not_7_out, not_8_out);
  and and_11 (and_11_out, xor_4_out, not_10_out);
  nor nor_4 (nor_4_out, buffer_4_out, and_12_out);
  and and_12 (and_12_out, not_9_out, not_10_out);
  nor nor_5 (nor_5_out, and_5_out, nor_1_out);
  buf buffer_1 (buffer_1_out, nor_5_out);
  nor nor_6 (nor_6_out, and_7_out, nor_2_out);
  buf buffer_2 (buffer_2_out, nor_6_out);
  nor nor_7 (nor_7_out, and_9_out, nor_3_out);
  buf buffer_3 (buffer_3_out, nor_7_out);
  nor nor_8 (nor_8_out, and_11_out, nor_4_out);
  buf buffer_4 (buffer_4_out, nor_8_out);
  and and_13 (and_13_out, nor_5_out, and_1_out);
  and and_14 (and_14_out, nor_1_out, and_1_out);
  and and_15 (and_15_out, nor_6_out, and_1_out);
  and and_16 (and_16_out, nor_2_out, and_1_out);
  and and_17 (and_17_out, nor_7_out, and_1_out);
  and and_18 (and_18_out, nor_3_out, and_1_out);
  and and_19 (and_19_out, nor_8_out, and_1_out);
  and and_20 (and_20_out, nor_4_out, and_1_out);
  or or_1 (or_1_out, and_13_out, CALC_out);
  nor nor_9 (Q, or_1_out, nor_10_out);
  buf buffer_5 (buffer_5_out, Q);
  nor nor_10 (nor_10_out, buffer_5_out, or_2_out);
  or or_2 (or_2_out, PRN_2, and_14_out);
  or or_3 (or_3_out, and_15_out, CALC_out);
  nor nor_11 (Q_4, or_3_out, nor_12_out);
  buf buffer_6 (buffer_6_out, Q_4);
  nor nor_12 (nor_12_out, buffer_6_out, or_4_out);
  or or_4 (or_4_out, PRN_4, and_16_out);
  or or_5 (or_5_out, and_17_out, CALC_out);
  nor nor_13 (Q_6, or_5_out, nor_14_out);
  buf buffer_7 (buffer_7_out, Q_6);
  nor nor_14 (nor_14_out, buffer_7_out, or_6_out);
  or or_6 (or_6_out, PRN_6, and_18_out);
  or or_7 (or_7_out, and_19_out, CALC_out);
  nor nor_15 (Q_8, or_7_out, nor_16_out);
  buf buffer_8 (buffer_8_out, Q_8);
  nor nor_16 (nor_16_out, buffer_8_out, or_8_out);
  or or_8 (or_8_out, PRN_8, and_20_out);
  and and_21 (and_21_out, Q, Q_4, Q_6, Q_8);
  buf buffer_9 (buffer_9_out, Q_8);
  buf buffer_10 (buffer_10_out, Q_6);
  buf buffer_11 (buffer_11_out, Q_4);
  buf buffer_12 (buffer_12_out, Q);
  not not_11 (not_11_out, buffer_9_out);
  not not_12 (not_12_out, buffer_10_out);
  not not_13 (not_13_out, buffer_11_out);
  not not_14 (not_14_out, buffer_12_out);
  and _0000 (_0000_out, not_11_out, not_12_out, not_13_out, not_14_out);
  and _0001 (_0001_out, not_11_out, not_12_out, not_13_out, buffer_12_out);
  and _0010 (_0010_out, not_11_out, not_12_out, buffer_11_out, not_14_out);
  and _0011 (_0011_out, not_11_out, not_12_out, buffer_11_out, buffer_12_out);
  and _0100 (_0100_out, not_11_out, buffer_10_out, not_13_out, not_14_out);
  and _0101 (_0101_out, not_11_out, buffer_10_out, not_13_out, buffer_12_out);
  and _0110 (_0110_out, not_11_out, buffer_10_out, buffer_11_out, not_14_out);
  and _0111 (_0111_out, not_11_out, buffer_10_out, buffer_11_out, buffer_12_out);
  and _1000 (_1000_out, buffer_9_out, not_12_out, not_13_out, not_14_out);
  and _1001 (_1001_out, buffer_9_out, not_12_out, not_13_out, buffer_12_out);
  and _1010 (_1010_out, buffer_9_out, not_12_out, buffer_11_out, not_14_out);
  and _1011 (_1011_out, buffer_9_out, not_12_out, buffer_11_out, buffer_12_out);
  and _1100 (_1100_out, buffer_9_out, buffer_10_out, not_13_out, not_14_out);
  and _1101 (_1101_out, buffer_9_out, buffer_10_out, not_13_out, buffer_12_out);
  and _1110 (_1110_out, buffer_9_out, buffer_10_out, buffer_11_out, not_14_out);
  and _1111 (_1111_out, buffer_9_out, buffer_10_out, buffer_11_out, buffer_12_out);
  Button CALC (.out(CALC_out));
  and and_22 (and_22_out, in_17, in_1);
  buf buffer_13 (buffer_13_out, _0000_out);
  buf buffer_14 (buffer_14_out, _0001_out);
  buf buffer_15 (buffer_15_out, _0010_out);
  buf buffer_16 (buffer_16_out, _0011_out);
  buf buffer_17 (buffer_17_out, _0100_out);
  buf buffer_18 (buffer_18_out, _0101_out);
  buf buffer_19 (buffer_19_out, _0110_out);
  buf buffer_20 (buffer_20_out, _0111_out);
  buf buffer_21 (buffer_21_out, _1000_out);
  buf buffer_22 (buffer_22_out, _1001_out);
  buf buffer_23 (buffer_23_out, _1010_out);
  buf buffer_24 (buffer_24_out, _1011_out);
  buf buffer_25 (buffer_25_out, _1100_out);
  buf buffer_26 (buffer_26_out, _1101_out);
  buf buffer_27 (buffer_27_out, _1110_out);
  buf buffer_28 (buffer_28_out, _1111_out);
  or or_9 (or_9_out, SUM_4, TOTAL);
  or or_10 (or_10_out, SUM_3, TOTAL);
  or or_11 (or_11_out, SUM_2, TOTAL);
  or or_12 (or_12_out, SUM, TOTAL);
  not not_15 (not_15_out, in_17);
  not not_16 (not_16_out, in_1);
  and and_23 (and_23_out, not_15_out, not_16_out);
  and and_24 (and_24_out, in_18, in_2);
  nor nor_17 (out_157, and_22_out, and_23_out);
  and and_25 (and_25_out, out_157, buffer_28_out);
  not not_17 (not_17_out, or_11_out);
  not not_18 (not_18_out, or_9_out);
  not not_19 (not_19_out, or_11_out);
  not not_20 (not_20_out, or_12_out);
  not not_21 (not_21_out, or_10_out);
  not not_22 (not_22_out, in_2);
  not not_23 (not_23_out, in_18);
  and and_26 (and_26_out, not_23_out, not_22_out);
  and and_27 (and_27_out, in_19, in_3);
  nor nor_18 (out_158, and_24_out, and_26_out);
  and and_28 (and_28_out, out_158, buffer_27_out);
  and and_29 (and_29_out, buffer_36_out, buffer_35_out, buffer_34_out, buffer_33_out);
  and and_30 (and_30_out, not_17_out, or_10_out);
  and and_31 (and_31_out, or_10_out, not_18_out);
  and and_32 (and_32_out, or_12_out, not_19_out);
  and and_33 (and_33_out, or_12_out, or_9_out);
  and and_34 (and_34_out, not_20_out, or_11_out, not_21_out);
  not not_24 (not_24_out, in_19);
  not not_25 (not_25_out, in_3);
  and and_35 (and_35_out, not_24_out, not_25_out);
  and and_36 (and_36_out, in_20, in_4);
  nor nor_19 (out_159, and_27_out, and_35_out);
  and and_37 (and_37_out, out_159, buffer_26_out);
  or or_13 (or_13_out, SUM, SUM_2, SUM_3, SUM_4);
  not not_26 (not_26_out, or_13_out);
  or or_14 (out_92, and_30_out, and_31_out, and_32_out, and_33_out, and_34_out);
  not not_27 (not_27_out, in_4);
  not not_28 (not_28_out, in_20);
  and and_38 (and_38_out, not_28_out, not_27_out);
  and and_39 (and_39_out, in_21, in_5);
  nor nor_20 (out_160, and_36_out, and_38_out);
  and and_40 (and_40_out, out_160, buffer_25_out);
  xor xor_5 (xor_5_out, GND, buffer_36_out);
  and and_41 (and_41_out, buffer_36_out, GND);
  and and_42 (TOTAL, and_29_out, not_26_out);
  not not_29 (not_29_out, in_5);
  not not_30 (not_30_out, in_21);
  and and_43 (and_43_out, not_30_out, not_29_out);
  and and_44 (and_44_out, in_22, in_6);
  nor nor_21 (out_161, and_39_out, and_43_out);
  and and_45 (and_45_out, out_161, buffer_24_out);
  xor xor_6 (SUM, xor_5_out, or_17_out);
  and and_46 (and_46_out, or_17_out, xor_5_out);
  or or_15 (or_15_out, and_46_out, and_41_out);
  not not_31 (not_31_out, or_10_out);
  not not_32 (not_32_out, or_9_out);
  not not_33 (not_33_out, or_9_out);
  not not_34 (not_34_out, or_11_out);
  not not_35 (not_35_out, or_12_out);
  not not_36 (not_36_out, or_10_out);
  not not_37 (not_37_out, in_6);
  not not_38 (not_38_out, in_22);
  and and_47 (and_47_out, not_38_out, not_37_out);
  and and_48 (and_48_out, in_23, in_7);
  nor nor_22 (out_162, and_44_out, and_47_out);
  and and_49 (and_49_out, out_162, buffer_23_out);
  and and_50 (and_50_out, not_31_out, not_32_out);
  and and_51 (and_51_out, or_11_out, not_33_out);
  and and_52 (and_52_out, or_12_out, not_34_out);
  and and_53 (and_53_out, or_12_out, or_10_out);
  and and_54 (and_54_out, not_35_out, or_11_out, not_36_out);
  not not_39 (not_39_out, in_7);
  not not_40 (not_40_out, in_23);
  and and_55 (and_55_out, not_40_out, not_39_out);
  and and_56 (and_56_out, in_24, in_8);
  nor nor_23 (out_163, and_48_out, and_55_out);
  and and_57 (and_57_out, out_163, buffer_22_out);
  and and_58 (and_58_out, buffer_35_out, GND);
  or or_16 (out_60, and_50_out, and_51_out, and_52_out, and_53_out, and_54_out);
  not not_41 (not_41_out, in_24);
  not not_42 (not_42_out, in_8);
  and and_59 (and_59_out, not_41_out, not_42_out);
  and and_60 (and_60_out, in_25, in_9);
  nor nor_24 (out_164, and_56_out, and_59_out);
  and and_61 (and_61_out, out_164, buffer_21_out);
  xor xor_7 (xor_7_out, GND, buffer_35_out);
  and and_62 (and_62_out, or_19_out, xor_7_out);
  not not_43 (not_43_out, or_11_out);
  not not_44 (not_44_out, or_9_out);
  not not_45 (not_45_out, or_9_out);
  not not_46 (not_46_out, in_25);
  not not_47 (not_47_out, in_9);
  and and_63 (and_63_out, not_46_out, not_47_out);
  and and_64 (and_64_out, in_26, in_10);
  nor nor_25 (out_165, and_60_out, and_63_out);
  and and_65 (and_65_out, out_165, buffer_20_out);
  xor xor_8 (SUM_2, xor_7_out, or_19_out);
  or or_17 (or_17_out, and_62_out, and_58_out);
  and and_66 (and_66_out, not_43_out, not_44_out);
  and and_67 (and_67_out, or_10_out, not_45_out);
  and and_68 (and_68_out, or_12_out, or_10_out);
  and and_69 (and_69_out, or_12_out, or_11_out);
  not not_48 (not_48_out, in_10);
  not not_49 (not_49_out, in_26);
  and and_70 (and_70_out, not_49_out, not_48_out);
  and and_71 (and_71_out, in_27, in_11);
  nor nor_26 (out_166, and_64_out, and_70_out);
  and and_72 (and_72_out, out_166, buffer_19_out);
  or or_18 (out_108, and_66_out, and_67_out, and_68_out, and_69_out);
  not not_50 (not_50_out, in_11);
  not not_51 (not_51_out, in_27);
  and and_73 (and_73_out, not_51_out, not_50_out);
  and and_74 (and_74_out, in_28, in_12);
  nor nor_27 (out_167, and_71_out, and_73_out);
  and and_75 (and_75_out, out_167, buffer_18_out);
  xor xor_9 (xor_9_out, GND, buffer_34_out);
  and and_76 (and_76_out, or_23_out, xor_9_out);
  and and_77 (and_77_out, buffer_34_out, GND);
  not not_52 (not_52_out, in_28);
  not not_53 (not_53_out, in_12);
  and and_78 (and_78_out, not_52_out, not_53_out);
  and and_79 (and_79_out, in_29, in_13);
  nor nor_28 (out_168, and_74_out, and_78_out);
  and and_80 (and_80_out, out_168, buffer_17_out);
  xor xor_10 (SUM_3, xor_9_out, or_23_out);
  or or_19 (or_19_out, and_76_out, and_77_out);
  not not_54 (not_54_out, or_10_out);
  not not_55 (not_55_out, or_12_out);
  not not_56 (not_56_out, or_11_out);
  not not_57 (not_57_out, or_9_out);
  not not_58 (not_58_out, or_11_out);
  not not_59 (not_59_out, or_10_out);
  not not_60 (not_60_out, or_9_out);
  not not_61 (not_61_out, in_13);
  not not_62 (not_62_out, in_29);
  and and_81 (and_81_out, not_62_out, not_61_out);
  and and_82 (and_82_out, in_30, in_14);
  nor nor_29 (out_169, and_79_out, and_81_out);
  and and_83 (and_83_out, out_169, buffer_16_out);
  and and_84 (and_84_out, or_12_out, not_54_out);
  and and_85 (and_85_out, not_55_out, not_56_out, not_57_out);
  and and_86 (and_86_out, not_58_out, or_10_out, or_9_out);
  and and_87 (and_87_out, or_11_out, not_59_out, or_9_out);
  and and_88 (and_88_out, or_11_out, or_10_out, not_60_out);
  not not_63 (not_63_out, in_14);
  not not_64 (not_64_out, in_30);
  and and_89 (and_89_out, not_64_out, not_63_out);
  and and_90 (and_90_out, in_31, in_15);
  nor nor_30 (out_170, and_82_out, and_89_out);
  and and_91 (and_91_out, out_170, buffer_15_out);
  or or_20 (or_20_out, and_28_out, and_37_out, and_40_out, and_45_out, and_49_out);
  xor xor_11 (xor_11_out, or_25_out, buffer_33_out);
  and and_92 (and_92_out, buffer_33_out, or_25_out);
  or or_21 (out_141, and_84_out, and_85_out, and_86_out, and_87_out, and_88_out);
  not not_65 (not_65_out, in_31);
  not not_66 (not_66_out, in_15);
  and and_93 (and_93_out, not_65_out, not_66_out);
  and and_94 (and_94_out, in_32, in_16);
  nor nor_31 (out_171, and_90_out, and_93_out);
  and and_95 (and_95_out, out_171, buffer_14_out);
  or or_22 (or_22_out, and_57_out, and_61_out, and_65_out, and_72_out, and_75_out);
  xor xor_12 (SUM_4, xor_11_out, in_39);
  and and_96 (and_96_out, in_39, xor_11_out);
  or or_23 (or_23_out, and_96_out, and_92_out);
  not not_67 (not_67_out, in_16);
  not not_68 (not_68_out, in_32);
  and and_97 (and_97_out, not_68_out, not_67_out);
  nor nor_32 (out_172, and_94_out, and_97_out);
  and and_98 (and_98_out, out_172, buffer_13_out);
  or or_24 (or_24_out, and_80_out, and_83_out, and_91_out, and_95_out, and_98_out);
  or or_25 (or_25_out, and_25_out, or_20_out, or_22_out, or_24_out);
  not not_69 (not_69_out, or_12_out);
  and and_99 (and_99_out, not_69_out, not_70_out);
  not not_70 (not_70_out, or_10_out);
  not not_71 (not_71_out, or_12_out);
  and and_100 (and_100_out, not_71_out, or_9_out);
  not not_72 (not_72_out, or_10_out);
  and and_101 (and_101_out, not_72_out, or_9_out);
  not not_73 (not_73_out, or_12_out);
  and and_102 (and_102_out, not_73_out, or_11_out);
  and and_103 (and_103_out, or_12_out, not_74_out);
  not not_74 (not_74_out, or_11_out);
  buf buffer_29 (buffer_29_out, SUM_4);
  buf buffer_30 (buffer_30_out, SUM_3);
  buf buffer_31 (buffer_31_out, SUM_2);
  buf buffer_32 (buffer_32_out, SUM);
  buf buffer_33 (buffer_33_out, Q_2);
  buf buffer_34 (buffer_34_out, Q_3);
  buf buffer_35 (buffer_35_out, Q_5);
  buf buffer_36 (buffer_36_out, Q_7);
  not not_75 (not_75_out, buffer_29_out);
  not not_76 (not_76_out, and_1_out);
  not not_77 (not_77_out, buffer_30_out);
  not not_78 (not_78_out, and_1_out);
  not not_79 (not_79_out, buffer_31_out);
  not not_80 (not_80_out, and_1_out);
  not not_81 (not_81_out, buffer_32_out);
  not not_82 (not_82_out, and_1_out);
  or or_26 (out_110, and_99_out, and_100_out, and_101_out, and_102_out, and_103_out);
  and and_104 (and_104_out, buffer_29_out, not_76_out);
  nor nor_33 (nor_33_out, buffer_37_out, and_105_out);
  and and_105 (and_105_out, not_75_out, not_76_out);
  and and_106 (and_106_out, buffer_30_out, not_78_out);
  nor nor_34 (nor_34_out, buffer_38_out, and_107_out);
  and and_107 (and_107_out, not_77_out, not_78_out);
  and and_108 (and_108_out, buffer_31_out, not_80_out);
  nor nor_35 (nor_35_out, buffer_39_out, and_109_out);
  and and_109 (and_109_out, not_79_out, not_80_out);
  and and_110 (and_110_out, buffer_32_out, not_82_out);
  nor nor_36 (nor_36_out, buffer_40_out, and_111_out);
  and and_111 (and_111_out, not_81_out, not_82_out);
  nor nor_37 (nor_37_out, and_104_out, nor_33_out);
  buf buffer_37 (buffer_37_out, nor_37_out);
  nor nor_38 (nor_38_out, and_106_out, nor_34_out);
  buf buffer_38 (buffer_38_out, nor_38_out);
  nor nor_39 (nor_39_out, and_108_out, nor_35_out);
  buf buffer_39 (buffer_39_out, nor_39_out);
  nor nor_40 (nor_40_out, and_110_out, nor_36_out);
  buf buffer_40 (buffer_40_out, nor_40_out);
  not not_83 (not_83_out, or_12_out);
  and and_112 (and_112_out, not_83_out, not_84_out);
  not not_84 (not_84_out, or_11_out);
  not not_85 (not_85_out, or_11_out);
  and and_113 (and_113_out, not_85_out, not_86_out);
  not not_86 (not_86_out, or_9_out);
  not not_87 (not_87_out, or_12_out);
  not not_88 (not_88_out, or_10_out);
  and and_114 (and_114_out, not_87_out, not_88_out, not_89_out);
  not not_89 (not_89_out, or_9_out);
  not not_90 (not_90_out, or_12_out);
  and and_115 (and_115_out, not_90_out, or_10_out, or_9_out);
  and and_116 (and_116_out, or_12_out, not_91_out, or_9_out);
  not not_91 (not_91_out, or_10_out);
  and and_117 (and_117_out, nor_37_out, and_1_out);
  and and_118 (and_118_out, nor_33_out, and_1_out);
  and and_119 (and_119_out, nor_38_out, and_1_out);
  and and_120 (and_120_out, nor_34_out, and_1_out);
  and and_121 (and_121_out, nor_39_out, and_1_out);
  and and_122 (and_122_out, nor_35_out, and_1_out);
  and and_123 (and_123_out, nor_40_out, and_1_out);
  and and_124 (and_124_out, nor_36_out, and_1_out);
  or or_27 (out_62, and_112_out, and_113_out, and_114_out, and_115_out, and_116_out);
  or or_28 (or_28_out, and_117_out, CALC_out);
  nor nor_41 (Q_2, or_28_out, nor_42_out);
  buf buffer_41 (buffer_41_out, Q_2);
  nor nor_42 (nor_42_out, buffer_41_out, or_29_out);
  or or_29 (or_29_out, PRN, and_118_out);
  or or_30 (or_30_out, and_119_out, CALC_out);
  nor nor_43 (Q_3, or_30_out, nor_44_out);
  buf buffer_42 (buffer_42_out, Q_3);
  nor nor_44 (nor_44_out, buffer_42_out, or_31_out);
  or or_31 (or_31_out, PRN_3, and_120_out);
  or or_32 (or_32_out, and_121_out, CALC_out);
  nor nor_45 (Q_5, or_32_out, nor_46_out);
  buf buffer_43 (buffer_43_out, Q_5);
  nor nor_46 (nor_46_out, buffer_43_out, or_33_out);
  or or_33 (or_33_out, PRN_5, and_122_out);
  or or_34 (or_34_out, and_123_out, CALC_out);
  nor nor_47 (Q_7, or_34_out, nor_48_out);
  buf buffer_44 (buffer_44_out, Q_7);
  nor nor_48 (nor_48_out, buffer_44_out, or_35_out);
  or or_35 (or_35_out, PRN_7, and_124_out);
  not not_92 (not_92_out, or_9_out);
  and and_125 (and_125_out, not_92_out, not_93_out);
  not not_93 (not_93_out, or_11_out);
  not not_94 (not_94_out, or_12_out);
  and and_126 (and_126_out, not_94_out, or_10_out);
  and and_127 (and_127_out, or_11_out, or_10_out);
  and and_128 (and_128_out, or_12_out, not_95_out);
  not not_95 (not_95_out, or_9_out);
  not not_96 (not_96_out, or_12_out);
  and and_129 (and_129_out, not_96_out, or_11_out, or_9_out);
  not not_97 (not_97_out, or_11_out);
  and and_130 (and_130_out, or_12_out, not_97_out, not_98_out);
  not not_98 (not_98_out, or_10_out);
  or or_36 (or_36_out, and_125_out, and_126_out, and_127_out, and_128_out, and_129_out);
  or or_37 (out_44, or_36_out, and_130_out);

  assign out_45 = out_44;
  assign out_46 = out_44;
  assign out_47 = out_44;
  assign out_48 = out_44;
  assign out_49 = out_44;
  assign out_50 = out_44;
  assign out_51 = out_44;
  assign out_52 = out_44;
  assign out_53 = out_44;
  assign out_54 = out_44;
  assign out_55 = out_44;
  assign out_56 = out_44;
  assign out_57 = out_44;
  assign out_58 = out_44;
  assign out_59 = out_44;
  assign out_61 = out_60;
  assign out_63 = out_62;
  assign out_64 = out_60;
  assign out_65 = out_60;
  assign out_66 = out_62;
  assign out_67 = out_62;
  assign out_68 = out_60;
  assign out_69 = out_60;
  assign out_70 = out_62;
  assign out_71 = out_62;
  assign out_72 = out_60;
  assign out_73 = out_60;
  assign out_74 = out_62;
  assign out_75 = out_62;
  assign out_76 = out_60;
  assign out_77 = out_60;
  assign out_78 = out_62;
  assign out_79 = out_62;
  assign out_80 = out_60;
  assign out_81 = out_60;
  assign out_82 = out_62;
  assign out_83 = out_62;
  assign out_84 = out_60;
  assign out_85 = out_60;
  assign out_86 = out_62;
  assign out_87 = out_62;
  assign out_88 = out_60;
  assign out_89 = out_60;
  assign out_90 = out_62;
  assign out_91 = out_62;
  assign out_93 = out_92;
  assign out_94 = out_92;
  assign out_95 = out_92;
  assign out_96 = out_92;
  assign out_97 = out_92;
  assign out_98 = out_92;
  assign out_99 = out_92;
  assign out_100 = out_92;
  assign out_101 = out_92;
  assign out_102 = out_92;
  assign out_103 = out_92;
  assign out_104 = out_92;
  assign out_105 = out_92;
  assign out_106 = out_92;
  assign out_107 = out_92;
  assign out_109 = out_108;
  assign out_111 = out_110;
  assign out_112 = out_108;
  assign out_113 = out_108;
  assign out_114 = out_110;
  assign out_115 = out_110;
  assign out_116 = out_108;
  assign out_117 = out_108;
  assign out_118 = out_110;
  assign out_119 = out_110;
  assign out_120 = out_108;
  assign out_121 = out_108;
  assign out_122 = out_110;
  assign out_123 = out_110;
  assign out_124 = out_108;
  assign out_125 = out_108;
  assign out_126 = out_110;
  assign out_127 = out_110;
  assign out_128 = out_108;
  assign out_129 = out_108;
  assign out_130 = out_110;
  assign out_131 = out_110;
  assign out_132 = out_108;
  assign out_133 = out_108;
  assign out_134 = out_110;
  assign out_135 = out_110;
  assign out_136 = out_108;
  assign out_137 = out_108;
  assign out_138 = out_110;
  assign out_139 = out_110;
  assign out_142 = out_141;
  assign out_143 = out_141;
  assign out_144 = out_141;
  assign out_145 = out_141;
  assign out_146 = out_141;
  assign out_147 = out_141;
  assign out_148 = out_141;
  assign out_149 = out_141;
  assign out_150 = out_141;
  assign out_151 = out_141;
  assign out_152 = out_141;
  assign out_153 = out_141;
  assign out_154 = out_141;
  assign out_155 = out_141;
  assign out_156 = out_141;
endmodule
